# Fritzing sketch BME280 (saved by Fritzing 0.9.3b)
breadboards: 1

parts:
  Composant1 = BME280 Breakout
  Composant2 = Arduino Pro Mini (3.3V)

nets:
  GND: Composant1.GND, Composant2.GND
  3.3V: Composant1.3.3V, Composant2.VCC
  N1: Composant1.SDI/SDA, Composant2.A4
  N2: Composant1.SCK/SCL, Composant2.A5
