# Fritzing sketch nRF24L01+ (saved by Fritzing 0.9.3b)
breadboards: 1

parts:
  Composant1 = Arduino Pro Mini (3.3V)
  Composant2 = NRF24L01+ Breakout Board

nets:
  GND: Composant1.GND, Composant2.GND
  VCC: Composant1.VCC, Composant2.VCC
  N1: Composant1.SCK, Composant2.SCK
  N2: Composant1.MISO, Composant2.MISO
  N3: Composant1.MOSI, Composant2.MOSI
  N4: Composant1.D10, Composant2.CS
  N5: Composant1.D9, Composant2.CE
  N6: Composant1.D8, Composant2.IRQ

notes:
  Les broches 9 (CE) et 10 (CS) sont deplaçable
  3.3V → VCC
  GND → GND
  D8 → IRQ
  D9 → CE
  D10 → CSN
  D11 → MOSI
  D12 → MISO
  D13 → SCK
